// Logisim project x69_lamda_b01.circ as structural Verilog: 2 circuits, main circuit main
module main (
);

  wire and_1_out, button_1_out, clock_1_out, por_1_out, s_r_ff_1_q, t_ff_1_q, t_ff_1_qn, t_ff_2_q, t_ff_2_qn,
       undriven, undriven_4;
  wire [3:0] undriven_3, undriven_5;
  wire [15:0] reg16_1_ro0, reg16_1_ro1, reg16_1_ro2, reg16_1_ro3, undriven_2;

  Button button_1 (.out(button_1_out));
  Clock clock_1 (.out(clock_1_out));
  POR #(.PorHighDuration(1)) por_1 (.out(por_1_out));
  T_Flip_Flop t_ff_1 (.clk(button_1_out), .T(1'b1), .Q(t_ff_1_q), .Qn(t_ff_1_qn), .reset(por_1_out));  // open: preset
  and and_1 (and_1_out, clock_1_out, s_r_ff_1_q);
  S_R_Flip_Flop s_r_ff_1 (
    .S(t_ff_1_q), .clk(clock_1_out), .R(t_ff_1_qn), .Q(s_r_ff_1_q), .reset(por_1_out));  // open: Qn, preset
  Reg16 reg16_1 (
    .Ro2(reg16_1_ro2), .Ro0(reg16_1_ro0), .Ro1(reg16_1_ro1), .Ro3(reg16_1_ro3), .DIn(undriven_2),
    .W(undriven_4), .En(t_ff_2_qn), .Wsel(undriven_3), .Rst(por_1_out), .Rs0(undriven_5), .Rs1(4'b0000),
    .Rs2(4'b0000), .Rs3(4'b0000));
  Reg16 reg16_2 (
    .Ro2(reg16_1_ro2), .Ro0(reg16_1_ro0), .Ro1(reg16_1_ro1), .Ro3(reg16_1_ro3), .DIn(undriven_2),
    .W(undriven_4), .En(t_ff_2_q), .Wsel(undriven_3), .Rst(por_1_out), .Rs0(undriven_5), .Rs1(4'b0000),
    .Rs2(4'b0000), .Rs3(4'b0000));
  T_Flip_Flop t_ff_2 (.clk(undriven), .T(1'b1), .Q(t_ff_2_q), .Qn(t_ff_2_qn), .reset(por_1_out));  // open: preset
  // Probe on reg16_1_ro0
  // Probe on reg16_1_ro1
  // Probe on reg16_1_ro2
  // Probe on reg16_1_ro3

  // Notes on the sheet:
  //   Interrupt
  //   Standard
endmodule

module Reg16 (
  input  [15:0] DIn,
  input  W,
  input  En,
  input  [3:0] Wsel,
  input  Rst,
  input  [3:0] Rs0,
  input  [3:0] Rs1,
  input  [3:0] Rs2,
  input  [3:0] Rs3,
  output [15:0] Ro0,
  output [15:0] Ro1,
  output [15:0] Ro2,
  output [15:0] Ro3
);

  wire decoder_1_out0, decoder_1_out1, decoder_1_out2, decoder_1_out3, decoder_1_out4, decoder_1_out5,
       decoder_1_out6, decoder_1_out7, decoder_1_out8, decoder_1_out9, decoder_1_out10, decoder_1_out11,
       decoder_1_out12, decoder_1_out13, decoder_1_out14, decoder_1_out15;
  wire [15:0] multiplexer_1_out, multiplexer_2_out, multiplexer_3_out, multiplexer_4_out, register_1_q,
       register_2_q, register_3_q, register_4_q, register_5_q, register_6_q, register_7_q, register_8_q,
       register_9_q, register_10_q, register_11_q, register_12_q, register_13_q, register_14_q,
       register_15_q, register_16_q;

  Decoder #(.select(4)) decoder_1 (
    .out0(decoder_1_out0), .out1(decoder_1_out1), .out2(decoder_1_out2), .out3(decoder_1_out3),
    .out4(decoder_1_out4), .out5(decoder_1_out5), .out6(decoder_1_out6), .out7(decoder_1_out7),
    .out8(decoder_1_out8), .out9(decoder_1_out9), .out10(decoder_1_out10), .out11(decoder_1_out11),
    .out12(decoder_1_out12), .out13(decoder_1_out13), .out14(decoder_1_out14), .out15(decoder_1_out15),
    .sel(Wsel), .en(En));
  Register #(.width(16)) register_1 (.D(DIn), .en(decoder_1_out0), .Q(register_1_q), .clk(W), .clr(Rst));
  Register #(.width(16)) register_2 (.D(DIn), .en(decoder_1_out1), .Q(register_2_q), .clk(W), .clr(Rst));
  Register #(.width(16)) register_3 (.D(DIn), .en(decoder_1_out2), .Q(register_3_q), .clk(W), .clr(Rst));
  Register #(.width(16)) register_4 (.D(DIn), .en(decoder_1_out3), .Q(register_4_q), .clk(W), .clr(Rst));
  Register #(.width(16)) register_5 (.D(DIn), .en(decoder_1_out4), .Q(register_5_q), .clk(W), .clr(Rst));
  Register #(.width(16)) register_6 (.D(DIn), .en(decoder_1_out5), .Q(register_6_q), .clk(W), .clr(Rst));
  Register #(.width(16)) register_7 (.D(DIn), .en(decoder_1_out6), .Q(register_7_q), .clk(W), .clr(Rst));
  Register #(.width(16)) register_8 (.D(DIn), .en(decoder_1_out7), .Q(register_8_q), .clk(W), .clr(Rst));
  Register #(.width(16)) register_9 (.D(DIn), .en(decoder_1_out8), .Q(register_9_q), .clk(W), .clr(Rst));
  Register #(.width(16)) register_10 (.D(DIn), .en(decoder_1_out9), .Q(register_10_q), .clk(W), .clr(Rst));
  Register #(.width(16)) register_11 (.D(DIn), .en(decoder_1_out10), .Q(register_11_q), .clk(W), .clr(Rst));
  Register #(.width(16)) register_12 (.D(DIn), .en(decoder_1_out11), .Q(register_12_q), .clk(W), .clr(Rst));
  Register #(.width(16)) register_13 (.D(DIn), .en(decoder_1_out12), .Q(register_13_q), .clk(W), .clr(Rst));
  Register #(.width(16)) register_14 (.D(DIn), .en(decoder_1_out13), .Q(register_14_q), .clk(W), .clr(Rst));
  Register #(.width(16)) register_15 (.D(DIn), .en(decoder_1_out14), .Q(register_15_q), .clk(W), .clr(Rst));
  Register #(.width(16)) register_16 (.D(DIn), .en(decoder_1_out15), .Q(register_16_q), .clk(W), .clr(Rst));
  Multiplexer #(.enable("false"), .select(4), .width(16)) multiplexer_1 (
    .in0(register_1_q), .in1(register_2_q), .in2(register_3_q), .in3(register_4_q), .in4(register_5_q),
    .in5(register_6_q), .in6(register_7_q), .in7(register_8_q), .in8(register_9_q), .in9(register_10_q),
    .in10(register_11_q), .in11(register_12_q), .in12(register_13_q), .in13(register_14_q),
    .in14(register_15_q), .in15(register_16_q), .out(multiplexer_1_out), .sel(Rs0));
  Multiplexer #(.enable("false"), .select(4), .width(16)) multiplexer_2 (
    .in0(register_1_q), .in1(register_2_q), .in2(register_3_q), .in3(register_4_q), .in4(register_5_q),
    .in5(register_6_q), .in6(register_7_q), .in7(register_8_q), .in8(register_9_q), .in9(register_10_q),
    .in10(register_11_q), .in11(register_12_q), .in12(register_13_q), .in13(register_14_q),
    .in14(register_15_q), .in15(register_16_q), .out(multiplexer_2_out), .sel(Rs1));
  Multiplexer #(.enable("false"), .select(4), .width(16)) multiplexer_3 (
    .in0(register_1_q), .in1(register_2_q), .in2(register_3_q), .in3(register_4_q), .in4(register_5_q),
    .in5(register_6_q), .in6(register_7_q), .in7(register_8_q), .in8(register_9_q), .in9(register_10_q),
    .in10(register_11_q), .in11(register_12_q), .in12(register_13_q), .in13(register_14_q),
    .in14(register_15_q), .in15(register_16_q), .out(multiplexer_3_out), .sel(Rs2));
  Multiplexer #(.enable("false"), .select(4), .width(16)) multiplexer_4 (
    .in0(register_1_q), .in1(register_2_q), .in2(register_3_q), .in3(register_4_q), .in4(register_5_q),
    .in5(register_6_q), .in6(register_7_q), .in7(register_8_q), .in8(register_9_q), .in9(register_10_q),
    .in10(register_11_q), .in11(register_12_q), .in12(register_13_q), .in13(register_14_q),
    .in14(register_15_q), .in15(register_16_q), .out(multiplexer_4_out), .sel(Rs3));
  assign Ro0 = En ? multiplexer_1_out : 16'bz;  // Controlled_Buffer controlled_buffer_1
  assign Ro1 = En ? multiplexer_2_out : 16'bz;  // Controlled_Buffer controlled_buffer_2
  assign Ro2 = En ? multiplexer_3_out : 16'bz;  // Controlled_Buffer controlled_buffer_3
  assign Ro3 = En ? multiplexer_4_out : 16'bz;  // Controlled_Buffer controlled_buffer_4
endmodule
